# Fritzing sketch kirakirakasa_wiring (saved by Fritzing 0.9.3b)

parts:
  Mod1 = Raspberry Pi Pico
  SD_card_module1 = SD Card Module
  S1 = Pushbutton [package="[THT]"]
  U1 = WS2812 RGB LED strip

nets:
  N1: Mod1.pin_6, U1.DIN
  N2: Mod1.pin_14, SD_card_module1.SCK
  N3: Mod1.pin_15, SD_card_module1.MOSI
  N4: Mod1.pin_16, SD_card_module1.MISO
  N5: Mod1.pin_17, SD_card_module1.CS
  N6: Mod1.pin_21, S1.Pin_3, S1.Pin_4
  GND: Mod1.pin_23, Mod1.pin_33, Mod1.pin_38, SD_card_module1.GND, S1.Pin_1, S1.Pin_2, U1.GND
  N7: Mod1.pin_39, SD_card_module1.+5, U1.VCC

custom parts:
  Raspberry Pi Pico: Raspberry Pi Pico. Based around the RP2040 microcontroller the Pico is a low cost microcontroller device bringing Raspberry Pi quality, cost, and easy of use to the microcontroller space. Jan 2021, Split part in to two versions: tht (this one) and SMD. This one will drill holes for a .1 in header in pcb to allow plugging in the module as well as providing pads to solder the module to the top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
  SD Card Module: SD Card Module Slot Socket Reader For Arduino ARM MCU
  WS2812 RGB LED strip: WS2812 strip
